// Logisim project DEMUX_NETWORK.circ as structural Verilog: 1 circuit, main circuit main
module main (
  input  D,
  input  S2,
  input  S1,
  input  S0,
  input  S2_2,
  input  S1_2,
  input  S0_2,
  input  S2_3,
  input  S1_3,
  input  S0_3,
  input  in_11,
  input  in_12,
  input  in_13,
  input  in_14,
  input  in_15,
  input  in_16,
  output O0,
  output O0_2,
  output O0_3,
  output O0_4,
  output O1,
  output O1_2,
  output O1_3,
  output O1_4,
  output O2,
  output O2_2,
  output O2_3,
  output O2_4,
  output O3,
  output O3_2,
  output O3_3,
  output O3_4,
  output O4,
  output O4_2,
  output O4_3,
  output O4_4,
  output O5,
  output O5_2,
  output O5_3,
  output O5_4,
  output O6,
  output O6_2,
  output O6_3,
  output O6_4,
  output O7,
  output O7_2,
  output O7_3,
  output O7_4
);

  wire and_1_out, and_2_out, and_3_out, and_4_out, and_5_out, and_6_out, and_7_out, and_8_out, not_1_out,
       not_2_out, not_3_out, not_4_out, not_5_out, not_6_out, not_7_out, not_8_out, not_9_out, not_10_out,
       not_11_out, not_12_out, not_13_out, not_14_out, not_15_out;

  not not_1 (not_1_out, S0);
  not not_2 (not_2_out, S2);
  not not_3 (not_3_out, S1);
  and and_1 (and_1_out, D, not_2_out, not_3_out, not_1_out);
  and and_2 (and_2_out, D, not_2_out, not_3_out, S0);
  and and_3 (and_3_out, D, not_2_out, S1, not_1_out);
  and and_4 (and_4_out, D, not_2_out, S1, S0);
  and and_5 (and_5_out, D, S2, not_3_out, not_1_out);
  and and_6 (and_6_out, D, S2, not_3_out, S0);
  and and_7 (and_7_out, D, S2, S1, not_1_out);
  and and_8 (and_8_out, D, S2, S1, S0);
  not not_4 (not_4_out, S1_2);
  not not_5 (not_5_out, S2_2);
  not not_6 (not_6_out, S0_2);
  and and_9 (O0, and_4_out, not_5_out, not_4_out, not_6_out);
  and and_10 (O1, and_4_out, not_5_out, not_4_out, S0_2);
  and and_11 (O2, and_4_out, not_5_out, S1_2, not_6_out);
  and and_12 (O3, and_4_out, not_5_out, S1_2, S0_2);
  and and_13 (O4, and_4_out, S2_2, not_4_out, not_6_out);
  and and_14 (O5, and_4_out, S2_2, not_4_out, S0_2);
  and and_15 (O6, and_4_out, S2_2, S1_2, not_6_out);
  and and_16 (O7, and_4_out, S2_2, S1_2, S0_2);
  not not_7 (not_7_out, S1_3);
  not not_8 (not_8_out, S2_3);
  not not_9 (not_9_out, S0_3);
  and and_17 (O0_2, and_3_out, not_8_out, not_7_out, not_9_out);
  and and_18 (O1_2, and_3_out, not_8_out, not_7_out, S0_3);
  and and_19 (O2_2, and_3_out, not_8_out, S1_3, not_9_out);
  and and_20 (O3_2, and_3_out, not_8_out, S1_3, S0_3);
  and and_21 (O4_2, and_3_out, S2_3, not_7_out, not_9_out);
  and and_22 (O5_2, and_3_out, S2_3, not_7_out, S0_3);
  and and_23 (O6_2, and_3_out, S2_3, S1_3, not_9_out);
  and and_24 (O7_2, and_3_out, S2_3, S1_3, S0_3);
  not not_10 (not_10_out, in_12);
  not not_11 (not_11_out, in_11);
  not not_12 (not_12_out, in_13);
  and and_25 (O0_3, and_2_out, not_11_out, not_10_out, not_12_out);
  and and_26 (O1_3, and_2_out, not_11_out, not_10_out, in_13);
  and and_27 (O2_3, and_2_out, not_11_out, in_12, not_12_out);
  and and_28 (O3_3, and_2_out, not_11_out, in_12, in_13);
  and and_29 (O4_3, and_2_out, in_11, not_10_out, not_12_out);
  and and_30 (O5_3, and_2_out, in_11, not_10_out, in_13);
  and and_31 (O6_3, and_2_out, in_11, in_12, not_12_out);
  and and_32 (O7_3, and_2_out, in_11, in_12, in_13);
  not not_13 (not_13_out, in_15);
  not not_14 (not_14_out, in_14);
  not not_15 (not_15_out, in_16);
  and and_33 (O0_4, and_1_out, not_14_out, not_13_out, not_15_out);
  and and_34 (O1_4, and_1_out, not_14_out, not_13_out, in_16);
  and and_35 (O2_4, and_1_out, not_14_out, in_15, not_15_out);
  and and_36 (O3_4, and_1_out, not_14_out, in_15, in_16);
  and and_37 (O4_4, and_1_out, in_14, not_13_out, not_15_out);
  and and_38 (O5_4, and_1_out, in_14, not_13_out, in_16);
  and and_39 (O6_4, and_1_out, in_14, in_15, not_15_out);
  and and_40 (O7_4, and_1_out, in_14, in_15, in_16);
endmodule
