// Logisim project DISPLAY.circ as structural Verilog: 2 circuits, main circuit main
module main (
  input  A4,
  input  A3,
  input  A2,
  input  A1,
  input  B4,
  input  B3,
  input  B2,
  input  B1
);

  wire and_1_out, and_2_out, and_3_out, and_4_out, and_5_out, and_6_out, and_7_out, and_8_out, and_9_out,
       and_10_out, and_11_out, and_12_out, and_13_out, and_14_out, and_15_out, and_16_out, and_17_out,
       and_18_out, and_19_out, and_20_out, and_21_out, and_22_out, and_23_out, and_24_out, and_25_out,
       and_26_out, and_27_out, and_28_out, display_1_a_2, display_1_b_2, display_1_c_2, display_1_d_2,
       display_1_e, display_1_g, not_1_out, not_2_out, not_3_out, not_4_out, not_5_out, not_6_out, not_7_out,
       not_8_out, not_9_out, not_10_out, not_11_out, not_12_out, not_13_out, not_14_out, not_15_out,
       not_16_out, not_17_out, not_18_out, not_19_out, not_20_out, not_21_out, not_22_out, not_23_out,
       not_24_out, or_1_out, or_2_out, or_3_out, or_4_out, or_5_out, or_6_out, or_7_out, or_8_out, undriven;

  not not_1 (not_1_out, A4);
  not not_2 (not_2_out, B4);
  not not_3 (not_3_out, A4);
  not not_4 (not_4_out, or_3_out);
  not not_5 (not_5_out, B4);
  not not_6 (not_6_out, or_3_out);
  DISPLAY display_1 (
    .A(or_2_out), .B(or_4_out), .C(or_6_out), .D(or_1_out), .a_2(display_1_a_2), .b_2(display_1_b_2),
    .c_2(display_1_c_2), .d_2(display_1_d_2), .e(display_1_e), .f(display_1_c_2), .g(display_1_g));
  and and_1 (and_1_out, not_1_out, not_2_out, or_3_out);
  and and_2 (and_2_out, not_3_out, B4, not_4_out);
  and and_3 (and_3_out, A4, not_5_out, not_6_out);
  and and_4 (and_4_out, A4, B4, or_3_out);
  and and_5 (and_5_out, B4, or_3_out);
  and and_6 (and_6_out, A4, or_3_out);
  and and_7 (and_7_out, A4, B4);
  LED led_1 (.in(or_1_out));
  or or_1 (or_1_out, and_5_out, and_6_out, and_7_out);
  or or_2 (or_2_out, and_1_out, and_2_out, and_3_out, and_4_out);
  not not_7 (not_7_out, A3);
  not not_8 (not_8_out, B3);
  not not_9 (not_9_out, A3);
  not not_10 (not_10_out, or_5_out);
  not not_11 (not_11_out, B3);
  not not_12 (not_12_out, or_5_out);
  and and_8 (and_8_out, B3, or_5_out);
  and and_9 (and_9_out, A3, or_5_out);
  and and_10 (and_10_out, A3, B3);
  _7_Segment_Display u_7_segment_display_1 (
    .g(display_1_g), .f(display_1_c_2), .a(display_1_a_2), .b(display_1_b_2), .e(display_1_e),
    .d(display_1_d_2), .c(display_1_c_2));  // open: dp
  and and_11 (and_11_out, not_7_out, not_8_out, or_5_out);
  and and_12 (and_12_out, not_9_out, B3, not_10_out);
  and and_13 (and_13_out, A3, not_11_out, not_12_out);
  and and_14 (and_14_out, A3, B3, or_5_out);
  LED led_2 (.in(or_3_out));
  or or_3 (or_3_out, and_8_out, and_9_out, and_10_out);
  or or_4 (or_4_out, and_11_out, and_12_out, and_13_out, and_14_out);
  not not_13 (not_13_out, A2);
  not not_14 (not_14_out, B2);
  not not_15 (not_15_out, A2);
  not not_16 (not_16_out, or_7_out);
  not not_17 (not_17_out, B2);
  not not_18 (not_18_out, or_7_out);
  and and_15 (and_15_out, B2, or_7_out);
  and and_16 (and_16_out, A2, or_7_out);
  and and_17 (and_17_out, A2, B2);
  and and_18 (and_18_out, not_13_out, not_14_out, or_7_out);
  and and_19 (and_19_out, not_15_out, B2, not_16_out);
  and and_20 (and_20_out, A2, not_17_out, not_18_out);
  and and_21 (and_21_out, A2, B2, or_7_out);
  LED led_3 (.in(or_5_out));
  or or_5 (or_5_out, and_15_out, and_16_out, and_17_out);
  or or_6 (or_6_out, and_18_out, and_19_out, and_20_out, and_21_out);
  not not_19 (not_19_out, A1);
  not not_20 (not_20_out, B1);
  not not_21 (not_21_out, A1);
  not not_22 (not_22_out, undriven);
  not not_23 (not_23_out, B1);
  not not_24 (not_24_out, undriven);
  and and_22 (and_22_out, not_19_out, not_20_out, undriven);
  and and_23 (and_23_out, not_21_out, B1, not_22_out);
  and and_24 (and_24_out, A1, not_23_out, not_24_out);
  and and_25 (and_25_out, A1, B1, undriven);
  and and_26 (and_26_out, B1, undriven);
  and and_27 (and_27_out, A1, undriven);
  and and_28 (and_28_out, A1, B1);
  LED led_4 (.in(or_7_out));
  or or_7 (or_7_out, and_26_out, and_27_out, and_28_out);
  LED led_5 (.in(or_2_out));
  LED led_6 (.in(or_1_out));
  or or_8 (or_8_out, and_22_out, and_23_out, and_24_out, and_25_out);
  LED led_7 (.in(or_8_out));
  LED led_8 (.in(or_4_out));
  LED led_9 (.in(or_6_out));

  // Notes on the sheet:
  //   CARRY OUT
  //   CARRY IN
  //   CARRY OUT
  //   CARRY IN
  //   CARRY IN
  //   CARRY OUT
  //   CARRY IN
  //   CARRY OUT
endmodule

module DISPLAY (
  input  A,
  input  B,
  input  C,
  input  D,
  output a_2,
  output b_2,
  output c_2,
  output d_2,
  output e,
  output f,
  output g
);

  wire and_1_out, and_2_out, and_3_out, and_4_out, and_5_out, and_6_out, and_7_out, and_8_out, and_9_out,
       and_10_out, and_11_out, and_12_out, and_13_out, and_14_out, and_15_out, and_16_out, and_17_out,
       and_18_out, not_1_out, not_2_out, not_3_out, not_4_out, not_5_out, not_6_out, not_7_out, not_8_out,
       not_9_out, not_10_out, not_11_out, not_12_out, not_13_out, not_14_out, not_15_out, not_16_out,
       not_17_out, not_18_out, not_19_out, not_20_out, not_21_out, not_22_out, not_23_out;

  not not_1 (not_1_out, B);
  and and_1 (and_1_out, not_1_out, not_2_out);
  not not_2 (not_2_out, D);
  not not_3 (not_3_out, B);
  and and_2 (and_2_out, not_3_out, C);
  and and_3 (and_3_out, B, D);
  not not_4 (not_4_out, B);
  not not_5 (not_5_out, C);
  and and_4 (and_4_out, not_5_out, not_6_out);
  not not_6 (not_6_out, D);
  and and_5 (and_5_out, C, D);
  not not_7 (not_7_out, C);
  or or_1 (c_2, not_7_out, D, B);
  not not_8 (not_8_out, B);
  and and_6 (and_6_out, not_8_out, not_9_out);
  not not_9 (not_9_out, D);
  not not_10 (not_10_out, B);
  and and_7 (and_7_out, not_10_out, C);
  and and_8 (and_8_out, C, not_11_out);
  not not_11 (not_11_out, D);
  and and_9 (and_9_out, B, not_12_out, D);
  not not_12 (not_12_out, C);
  not not_13 (not_13_out, B);
  and and_10 (and_10_out, not_13_out, not_14_out);
  not not_14 (not_14_out, D);
  and and_11 (and_11_out, C, not_15_out);
  not not_15 (not_15_out, D);
  and and_12 (and_12_out, A, not_16_out);
  not not_16 (not_16_out, D);
  not not_17 (not_17_out, C);
  and and_13 (and_13_out, not_17_out, not_18_out);
  not not_18 (not_18_out, D);
  and and_14 (and_14_out, B, not_19_out);
  not not_19 (not_19_out, C);
  and and_15 (and_15_out, B, not_20_out);
  not not_20 (not_20_out, D);
  not not_21 (not_21_out, B);
  and and_16 (and_16_out, not_21_out, C);
  and and_17 (and_17_out, B, not_22_out);
  not not_22 (not_22_out, C);
  and and_18 (and_18_out, B, not_23_out);
  not not_23 (not_23_out, D);
  or or_2 (a_2, and_1_out, and_2_out, and_3_out);
  or or_3 (b_2, not_4_out, and_4_out, and_5_out);
  or or_4 (d_2, and_6_out, and_7_out, and_8_out, and_9_out);
  or or_5 (e, and_10_out, and_11_out, and_12_out);
  or or_6 (f, and_13_out, and_14_out, and_15_out);
  or or_7 (g, and_16_out, and_17_out, and_18_out, A);
  _7_Segment_Display u_7_segment_display_1 (.g(g), .f(f), .a(a_2), .b(b_2), .e(e), .d(d_2), .c(c_2));  // open: dp
endmodule
