// Logisim project MUX.circ as structural Verilog: 1 circuit, main circuit main
module main (
  input  s0,
  input  s1,
  input  s2,
  input  _0,
  input  _1,
  input  _2,
  input  _3,
  input  _4,
  input  _5,
  input  _6,
  input  in_11,
  output out_12
);

  wire and_1_out, and_2_out, and_3_out, and_4_out, and_5_out, and_6_out, and_7_out, and_8_out, not_1_out,
       not_2_out, not_3_out;

  not not_1 (not_1_out, s0);
  not not_2 (not_2_out, s1);
  not not_3 (not_3_out, s2);
  and and_1 (and_1_out, _0, not_3_out, not_2_out, not_1_out);
  and and_2 (and_2_out, _1, not_3_out, not_2_out, s0);
  and and_3 (and_3_out, _2, not_3_out, s1, not_1_out);
  and and_4 (and_4_out, _3, not_3_out, s1, s0);
  and and_5 (and_5_out, _4, s2, not_2_out, not_1_out);
  and and_6 (and_6_out, _5, s2, not_2_out, s0);
  and and_7 (and_7_out, _6, s2, s1, not_1_out);
  and and_8 (and_8_out, in_11, s2, s1, s0);
  or or_1 (out_12, and_1_out, and_2_out, and_3_out, and_4_out, and_5_out, and_6_out, and_7_out, and_8_out);
endmodule
