// Logisim project PROJETO_IC_ALU.circ as structural Verilog: 11 circuits, main circuit main
module main (
  input  _2,
  input  _1,
  input  _2_2,
  input  _1_2,
  output _8,
  output _4,
  output _2_3,
  output _1_3
);

  // MULTIPLICADOR multiplicador_1: pin names not known; wires that end beside it: _2, _2_2, _1, _1_2, _8, _4, _2_3, _1_3
  ALU alu_1 ();  // open: in_1, in_3, in_5, in_6, in_9, in_11, in_13, in_15, out_21, out_23, out_26, out_28, out_30, in_17, in_18, in_19, in_20, out_31, out_32, out_33, out_34, out_22, out_24, out_25, out_27, out_29, in_2, in_4, in_7, in_8, in_10, in_12, in_14, in_16
endmodule

module FULL_ADDER (
  input  in_1,
  input  in_2,
  input  in_3,
  output out_4,
  output out_5
);

  wire and_1_out, and_2_out, and_3_out, and_4_out, and_5_out, and_6_out, and_7_out, not_1_out, not_2_out,
       not_3_out, not_4_out, not_5_out, not_6_out;

  not not_1 (not_1_out, in_1);
  not not_2 (not_2_out, in_2);
  not not_3 (not_3_out, in_1);
  not not_4 (not_4_out, in_3);
  not not_5 (not_5_out, in_2);
  not not_6 (not_6_out, in_3);
  and and_1 (and_1_out, in_2, in_3);
  and and_2 (and_2_out, in_1, in_3);
  and and_3 (and_3_out, in_1, in_2);
  and and_4 (and_4_out, not_1_out, not_2_out, in_3);
  and and_5 (and_5_out, not_3_out, in_2, not_4_out);
  and and_6 (and_6_out, in_1, not_5_out, not_6_out);
  and and_7 (and_7_out, in_1, in_2, in_3);
  or or_1 (out_5, and_1_out, and_2_out, and_3_out);
  or or_2 (out_4, and_4_out, and_5_out, and_6_out, and_7_out);
endmodule

module FULL_SUBTRACTOR (
  input  A,
  input  B,
  input  Bin,
  output DIFF,
  output Bout
);

  wire and_1_out, and_2_out, and_3_out, and_4_out, and_5_out, and_6_out, and_7_out, not_1_out, not_2_out,
       not_3_out, not_4_out, not_5_out, not_6_out, not_7_out, not_8_out;

  not not_1 (not_1_out, A);
  not not_2 (not_2_out, B);
  not not_3 (not_3_out, A);
  not not_4 (not_4_out, Bin);
  not not_5 (not_5_out, B);
  not not_6 (not_6_out, Bin);
  not not_7 (not_7_out, A);
  not not_8 (not_8_out, A);
  and and_1 (and_1_out, not_1_out, not_2_out, Bin);
  and and_2 (and_2_out, not_3_out, B, not_4_out);
  and and_3 (and_3_out, A, not_5_out, not_6_out);
  and and_4 (and_4_out, A, B, Bin);
  and and_5 (and_5_out, not_7_out, Bin);
  and and_6 (and_6_out, not_8_out, B);
  and and_7 (and_7_out, B, Bin);
  or or_1 (DIFF, and_1_out, and_2_out, and_3_out, and_4_out);
  or or_2 (Bout, and_5_out, and_6_out, and_7_out);
endmodule

module MULTIPLICADOR (
  input  A1,
  input  A0,
  input  B1,
  input  B0,
  output S4,
  output S3,
  output S2,
  output S1
);

  wire and_2_out, and_3_out, and_4_out, and_5_out, and_6_out, and_7_out, not_1_out, not_2_out, not_3_out,
       not_4_out, not_5_out, not_6_out;

  and and_1 (S4, A1, A0, B1, B0);
  and and_2 (and_2_out, A1, not_1_out, B1);
  not not_1 (not_1_out, A0);
  and and_3 (and_3_out, A1, B1, not_2_out);
  not not_2 (not_2_out, B0);
  not not_3 (not_3_out, A1);
  and and_4 (and_4_out, not_3_out, A0, B1);
  and and_5 (and_5_out, A0, B1, not_4_out);
  not not_4 (not_4_out, B0);
  not not_5 (not_5_out, A0);
  and and_6 (and_6_out, A1, not_5_out, B0);
  not not_6 (not_6_out, B1);
  and and_7 (and_7_out, A1, not_6_out, B0);
  and and_8 (S1, A0, B0);
  or or_1 (S3, and_2_out, and_3_out);
  or or_2 (S2, and_4_out, and_5_out, and_6_out, and_7_out);

  // Notes on the sheet:
  //   2
  //   1
  //   2
  //   1
  //   8
  //   4
  //   2
  //   1
endmodule

module ALU (
  input  in_1,
  input  in_2,
  input  in_3,
  input  in_4,
  input  in_5,
  input  in_6,
  input  in_7,
  input  in_8,
  input  in_9,
  input  in_10,
  input  in_11,
  input  in_12,
  input  in_13,
  input  in_14,
  input  in_15,
  input  in_16,
  input  in_17,
  input  in_18,
  input  in_19,
  input  in_20,
  output out_21,
  output out_22,
  output out_23,
  output out_24,
  output out_25,
  output out_26,
  output out_27,
  output out_28,
  output out_29,
  output out_30,
  output out_31,
  output out_32,
  output out_33,
  output out_34
);

  _4BIT_FULL_ADDER u_4bit_full_adder_1 (
    ._8(in_1), ._4(in_3), ._2(in_5), ._1(in_6), ._8_2(in_9), ._4_2(in_11), ._2_2(in_13), ._1_2(in_15),
    ._8_3(out_23), ._4_3(out_26), ._2_3(out_28), ._1_3(out_30), ._16(out_21));
  MULTIPLICADOR multiplicador_1 (
    .A1(in_17), .A0(in_18), .B1(in_19), .B0(in_20), .S4(out_31), .S3(out_32), .S2(out_33), .S1(out_34));
  _4BIT_FULL_SUBTRACTOR u_4bit_full_subtractor_1 (
    ._8(out_22), ._4(out_25), ._2(out_27), ._1(out_29), .A3(in_2), .A2(in_4), .A1(in_7), .A0(in_8),
    .B3(in_10), .B2(in_12), .B1(in_14), .B0(in_16), ._16(out_24));
  FULL_DIVIDER full_divider_1 ();  // open: A, B, Q, R
endmodule

module _4BIT_FULL_ADDER (
  input  _8,
  input  _4,
  input  _2,
  input  _1,
  input  _8_2,
  input  _4_2,
  input  _2_2,
  input  _1_2,
  output _16,
  output _8_3,
  output _4_3,
  output _2_3,
  output _1_3
);

  wire full_adder_2_out_5, full_adder_3_out_5, full_adder_4_out_5;

  FULL_ADDER full_adder_1 (.in_1(_8), .in_2(_8_2), .in_3(full_adder_2_out_5), .out_4(_8_3), .out_5(_16));
  FULL_ADDER full_adder_2 (.in_1(_4), .in_2(_4_2), .in_3(full_adder_3_out_5), .out_4(_4_3), .out_5(full_adder_2_out_5));
  FULL_ADDER full_adder_3 (.in_1(_2), .in_2(_2_2), .in_3(full_adder_4_out_5), .out_4(_2_3), .out_5(full_adder_3_out_5));
  FULL_ADDER full_adder_4 (.in_1(_1), .in_2(_1_2), .in_3(1'b0), .out_4(_1_3), .out_5(full_adder_4_out_5));
endmodule

module _4BIT_FULL_SUBTRACTOR (
  input  A3,
  input  A2,
  input  A1,
  input  A0,
  input  B3,
  input  B2,
  input  B1,
  input  B0,
  output _16,
  output _8,
  output _4,
  output _2,
  output _1
);

  wire full_subtractor_2_bout, full_subtractor_3_bout, full_subtractor_4_bout;

  FULL_SUBTRACTOR full_subtractor_1 (.A(A3), .B(B3), .Bin(full_subtractor_2_bout), .DIFF(_8), .Bout(_16));
  FULL_SUBTRACTOR full_subtractor_2 (
    .A(A2), .B(B2), .Bin(full_subtractor_3_bout), .DIFF(_4), .Bout(full_subtractor_2_bout));
  FULL_SUBTRACTOR full_subtractor_3 (
    .A(A1), .B(B1), .Bin(full_subtractor_4_bout), .DIFF(_2), .Bout(full_subtractor_3_bout));
  FULL_SUBTRACTOR full_subtractor_4 (.A(A0), .B(B0), .Bin(1'b0), .DIFF(_1), .Bout(full_subtractor_4_bout));

  // Notes on the sheet:
  //   8
  //   4
  //   2
  //   1
  //   8
  //   4
  //   2
  //   1
endmodule

module _2BIT_FULL_MULTIPLIER (
);

  MULTIPLICADOR multiplicador_1 ();  // open: A1, A0, B1, B0, S4, S3, S2, S1
endmodule

module _4BIT_DIVIDER (
  input  CI,
  input  R,
  input  B,
  output CO,
  output D
);

  wire and_1_out, and_2_out, and_3_out, xor_1_out;

  and and_1 (and_1_out, R, B);
  and and_2 (and_2_out, R, CI);
  and and_3 (and_3_out, B, CI);
  xor xor_1 (xor_1_out, R, B);
  or or_1 (CO, and_1_out, and_2_out, and_3_out);
  xor xor_2 (D, CI, xor_1_out);
endmodule

module FULL_DIVIDER (
  input  [3:0] A,
  input  [3:0] B,
  output [3:0] Q,
  output [3:0] R
);

  wire full_divider_stage2_1_d, full_divider_stage2_1_nb_2, full_divider_stage2_2_d,
       full_divider_stage2_2_nb_2, full_divider_stage2_3_d, full_divider_stage2_3_nb_2,
       full_divider_stage2_4_d, full_divider_stage2_5_co, full_divider_stage2_5_nb_2,
       full_divider_stage2_5_out_7, full_divider_stage2_6_co, full_divider_stage2_6_nb_2,
       full_divider_stage2_6_out_7, full_divider_stage2_7_co, full_divider_stage2_7_nb_2,
       full_divider_stage2_7_out_7, full_divider_stage2_8_co, full_divider_stage2_9_co,
       full_divider_stage2_9_nb_2, full_divider_stage2_9_out_7, full_divider_stage2_10_co,
       full_divider_stage2_10_nb_2, full_divider_stage2_10_out_7, full_divider_stage2_11_co,
       full_divider_stage2_11_nb_2, full_divider_stage2_11_out_7, full_divider_stage2_12_co,
       full_divider_stage2_13_co, full_divider_stage2_13_nb_2, full_divider_stage2_13_out_7,
       full_divider_stage2_14_co, full_divider_stage2_14_nb_2, full_divider_stage2_14_out_7,
       full_divider_stage2_15_co, full_divider_stage2_15_nb_2, full_divider_stage2_15_out_7,
       full_divider_stage2_16_co, not_1_out, not_2_out, not_3_out, not_4_out;

  not not_1 (not_1_out, B[0]);
  not not_2 (not_2_out, B[1]);
  not not_3 (not_3_out, B[2]);
  not not_4 (not_4_out, B[3]);
  not not_5 (Q[3], full_divider_stage2_1_d);
  not not_6 (Q[0], full_divider_stage2_4_d);
  not not_7 (Q[2], full_divider_stage2_2_d);
  not not_8 (Q[1], full_divider_stage2_3_d);
  FULL_DIVIDER_STAGE2 full_divider_stage2_1 (
    .N(full_divider_stage2_1_d), .in_3(full_divider_stage2_5_co), .R(1'b0), .nB(not_4_out),
    .nB_2(full_divider_stage2_1_nb_2), .D(full_divider_stage2_1_d));  // open: out_7, CO
  FULL_DIVIDER_STAGE2 full_divider_stage2_2 (
    .N(full_divider_stage2_2_d), .in_3(full_divider_stage2_6_co), .R(full_divider_stage2_5_out_7),
    .nB(full_divider_stage2_1_nb_2), .nB_2(full_divider_stage2_2_nb_2), .D(full_divider_stage2_2_d));  // open: out_7, CO
  FULL_DIVIDER_STAGE2 full_divider_stage2_3 (
    .N(full_divider_stage2_3_d), .in_3(full_divider_stage2_7_co), .R(full_divider_stage2_6_out_7),
    .nB(full_divider_stage2_2_nb_2), .nB_2(full_divider_stage2_3_nb_2), .D(full_divider_stage2_3_d));  // open: out_7, CO
  FULL_DIVIDER_STAGE2 full_divider_stage2_4 (
    .N(full_divider_stage2_4_d), .in_3(full_divider_stage2_8_co), .R(full_divider_stage2_7_out_7),
    .nB(full_divider_stage2_3_nb_2), .out_7(R[3]), .D(full_divider_stage2_4_d));  // open: nB_2, CO
  FULL_DIVIDER_STAGE2 full_divider_stage2_5 (
    .N(full_divider_stage2_1_d), .in_3(full_divider_stage2_9_co), .R(1'b0), .nB(not_3_out),
    .out_7(full_divider_stage2_5_out_7), .nB_2(full_divider_stage2_5_nb_2), .CO(full_divider_stage2_5_co));  // open: D
  FULL_DIVIDER_STAGE2 full_divider_stage2_6 (
    .N(full_divider_stage2_2_d), .in_3(full_divider_stage2_10_co), .R(full_divider_stage2_9_out_7),
    .nB(full_divider_stage2_5_nb_2), .out_7(full_divider_stage2_6_out_7), .nB_2(full_divider_stage2_6_nb_2),
    .CO(full_divider_stage2_6_co));  // open: D
  FULL_DIVIDER_STAGE2 full_divider_stage2_7 (
    .N(full_divider_stage2_3_d), .in_3(full_divider_stage2_11_co), .R(full_divider_stage2_10_out_7),
    .nB(full_divider_stage2_6_nb_2), .out_7(full_divider_stage2_7_out_7), .nB_2(full_divider_stage2_7_nb_2),
    .CO(full_divider_stage2_7_co));  // open: D
  FULL_DIVIDER_STAGE2 full_divider_stage2_8 (
    .N(full_divider_stage2_4_d), .in_3(full_divider_stage2_12_co), .R(full_divider_stage2_11_out_7),
    .nB(full_divider_stage2_7_nb_2), .out_7(R[2]), .CO(full_divider_stage2_8_co));  // open: nB_2, D
  FULL_DIVIDER_STAGE2 full_divider_stage2_9 (
    .N(full_divider_stage2_1_d), .in_3(full_divider_stage2_13_co), .R(1'b0), .nB(not_2_out),
    .out_7(full_divider_stage2_9_out_7), .nB_2(full_divider_stage2_9_nb_2), .CO(full_divider_stage2_9_co));  // open: D
  FULL_DIVIDER_STAGE2 full_divider_stage2_10 (
    .N(full_divider_stage2_2_d), .in_3(full_divider_stage2_14_co), .R(full_divider_stage2_13_out_7),
    .nB(full_divider_stage2_9_nb_2), .out_7(full_divider_stage2_10_out_7),
    .nB_2(full_divider_stage2_10_nb_2), .CO(full_divider_stage2_10_co));  // open: D
  FULL_DIVIDER_STAGE2 full_divider_stage2_11 (
    .N(full_divider_stage2_3_d), .in_3(full_divider_stage2_15_co), .R(full_divider_stage2_14_out_7),
    .nB(full_divider_stage2_10_nb_2), .out_7(full_divider_stage2_11_out_7),
    .nB_2(full_divider_stage2_11_nb_2), .CO(full_divider_stage2_11_co));  // open: D
  FULL_DIVIDER_STAGE2 full_divider_stage2_12 (
    .N(full_divider_stage2_4_d), .in_3(full_divider_stage2_16_co), .R(full_divider_stage2_15_out_7),
    .nB(full_divider_stage2_11_nb_2), .out_7(R[1]), .CO(full_divider_stage2_12_co));  // open: nB_2, D
  FULL_DIVIDER_STAGE2 full_divider_stage2_13 (
    .N(full_divider_stage2_1_d), .in_3(1'b1), .R(A[3]), .nB(not_1_out), .out_7(full_divider_stage2_13_out_7),
    .nB_2(full_divider_stage2_13_nb_2), .CO(full_divider_stage2_13_co));  // open: D
  FULL_DIVIDER_STAGE2 full_divider_stage2_14 (
    .N(full_divider_stage2_2_d), .in_3(1'b1), .R(A[2]), .nB(full_divider_stage2_13_nb_2),
    .out_7(full_divider_stage2_14_out_7), .nB_2(full_divider_stage2_14_nb_2), .CO(full_divider_stage2_14_co));  // open: D
  FULL_DIVIDER_STAGE2 full_divider_stage2_15 (
    .N(full_divider_stage2_3_d), .in_3(1'b1), .R(A[1]), .nB(full_divider_stage2_14_nb_2),
    .out_7(full_divider_stage2_15_out_7), .nB_2(full_divider_stage2_15_nb_2), .CO(full_divider_stage2_15_co));  // open: D
  FULL_DIVIDER_STAGE2 full_divider_stage2_16 (
    .N(full_divider_stage2_4_d), .in_3(1'b1), .R(A[0]), .nB(full_divider_stage2_15_nb_2), .out_7(R[0]),
    .CO(full_divider_stage2_16_co));  // open: nB_2, D
endmodule

module FULL_DIVIDER_STAGE2 (
  input  R,
  input  nB,
  input  in_3,
  input  N,
  output CO,
  output D,
  output out_7,
  output nB_2
);

  _4BIT_DIVIDER u_4bit_divider_1 (.CI(in_3), .CO(CO), .D(D), .R(R), .B(nB));
  Multiplexer multiplexer_1 (.in0(D), .in1(R), .out(out_7), .sel(N));  // open: en

  assign nB_2 = nB;

  // Notes on the sheet:
  //   R' 
endmodule
